// Digital circuit cpu.dig as structural Verilog
module cpu (
  input  Clock,
  input  PC_inc,
  input  PC_r,
  input  PC_w,
  input  IRH_w,
  input  IRL_w,
  input  DIR_sel,
  input  IMM_sel,
  input  Rs_src,
  input  Rd_w,
  input  Rs_r,
  input  IND_sel,
  input  SPC_r,
  input  SPC_w,
  input  RAM_r,
  input  RAM_w,
  input  ALU_r,
  input  HLT
);

  wire alu_1_c_o, alu_1_z_o, CLK, instruction_1_nst, status_1_c_o;
  wire [2:0] instruction_1_r_d, instruction_1_r_s0, instruction_1_r_s1;
  wire [4:0] instruction_1_opc;
  wire [7:0] ramsingleport_1_d, registers_1_alu_0, registers_1_alu_1;
  wire [15:0] pc_1_a_out;

  and and_1 (CLK, Clock, ~HLT);  // And
  pc pc_1 (.PC_inc(PC_inc), .CLK(CLK), .PC_r(PC_r), .PC_w(PC_w), .A_in(pc_1_a_out), .RST(1'b0), .A_out(pc_1_a_out));
  RAMSinglePort #(.AddrBits(16), .Bits(8)) ramsingleport_1 (
    .A(pc_1_a_out), .str(RAM_w), .C(CLK), .ld(RAM_r), .D(ramsingleport_1_d));
  instruction instruction_1 (
    .D_in(ramsingleport_1_d), .CLK(CLK), .IRH_w(IRH_w), .IRL_w(IRL_w), .DIR_sel(DIR_sel), .IMM_sel(IMM_sel),
    .Rs_src(Rs_src), .A_out(pc_1_a_out), .D_out(ramsingleport_1_d), .R_d(instruction_1_r_d),
    .R_S0(instruction_1_r_s0), .R_S1(instruction_1_r_s1), .nSt(instruction_1_nst), .OPC(instruction_1_opc));
  registers registers_1 (
    .A_in(pc_1_a_out), .D_in(ramsingleport_1_d), .CLK(CLK), .Rd(instruction_1_r_d), .Rd_w(Rd_w),
    .nSt(instruction_1_nst), .R_S0(instruction_1_r_s0), .Rs_r(Rs_r), .R_S1(instruction_1_r_s1),
    .DIR_sel(DIR_sel), .IND_sel(IND_sel), .SPC_r(SPC_r), .SPC_w(SPC_w), .A_out(pc_1_a_out),
    .D_out(ramsingleport_1_d), .ALU_0(registers_1_alu_0), .ALU_1(registers_1_alu_1));
  alu alu_1 (
    .ALU_0(registers_1_alu_0), .ALU_1(registers_1_alu_1), .OPC(instruction_1_opc), .C_i(status_1_c_o),
    .ALU_r(ALU_r), .D_o(ramsingleport_1_d), .Z_o(alu_1_z_o), .C_o(alu_1_c_o));  // open: CMP
  status status_1 (.Z_i(alu_1_z_o), .C_i(alu_1_c_o), .en(ALU_r), .CLK(CLK), .C_o(status_1_c_o));  // open: Z_o

  // Notes on the sheet:
  //   Rd_w: Write to destination register
  //   Rs_r: Read from source register
endmodule
